# Fritzing sketch oled&sensor block (saved by Fritzing 1.0.7)
stripboards: 1

parts:
  oled = female pin header, 4 pins [form="♀ (female)"]
  i2c = male pin header, 4 pins [form="♂ (male)"]
  converter_in = female pin header, 4 pins [form="♀ (female)"]
  converter_out_5 = female pin header, 4 pins [form="♀ (female)"]
  ads = female pin header, 6 pins [form="♀ (female)"]
  J2 = Screw terminal - 2 pins [package=THT]

nets:
  GND: oled.pin1, i2c.pin1, converter_in.pin1
  VCC: oled.pin2, i2c.pin2, converter_in.pin2
  SCL: oled.pin3, i2c.pin3, converter_in.pin3
  SDA: oled.pin4, i2c.pin4, converter_in.pin4
  GND5: converter_out_5.pin1, ads.pin2, J2.pin1
  VDD5: converter_out_5.pin2, ads.pin1, J2.pin2
  N1: converter_out_5.pin3, ads.pin3
  N2: converter_out_5.pin4, ads.pin4
